// Logisim project adder.circ as structural Verilog: 3 circuits, main circuit top
module main (
  input  in_1,
  input  in_2,
  input  in_3,
  output out_4,
  output out_5
);

  wire and_1_out, and_2_out, and_3_out;

  xor xor_1 (out_5, in_1, in_2, in_3);
  and and_1 (and_1_out, in_1, in_2);
  and and_2 (and_2_out, in_1, in_3);
  and and_3 (and_3_out, in_2, in_3);
  or or_1 (out_4, and_1_out, and_2_out, and_3_out);
endmodule

module top (
  input  in_1,
  input  in_2,
  input  in_3,
  input  in_4,
  input  in_5,
  input  in_6,
  input  in_7,
  input  in_8,
  output out_9,
  output out_10,
  output out_11,
  output out_12,
  output out_13
);

  wire main_2_out_4, main_3_out_4, main_4_out_4;

  main main_1 (.in_1(in_1), .in_2(in_5), .in_3(main_2_out_4), .out_4(out_9), .out_5(out_10));
  main main_2 (.in_1(in_2), .in_2(in_6), .in_3(main_3_out_4), .out_4(main_2_out_4), .out_5(out_11));
  main main_3 (.in_1(in_3), .in_2(in_7), .in_3(main_4_out_4), .out_4(main_3_out_4), .out_5(out_12));
  main main_4 (.in_1(in_4), .in_2(in_8), .in_3(1'b0), .out_4(main_4_out_4), .out_5(out_13));
endmodule

module flipper (
  input  in_1,
  input  in_2,
  input  in_3,
  input  in_4
);

  wire undriven, undriven_2, undriven_3, undriven_4;

  // XOR_Gate xor_1 has open pins: in0=in_1, in1=undriven, out=open
  // XOR_Gate xor_2 has open pins: in0=in_2, in1=undriven_2, out=open
  // XOR_Gate xor_3 has open pins: in0=in_3, in1=undriven_3, out=open
  // XOR_Gate xor_4 has open pins: in0=in_4, in1=undriven_4, out=open
endmodule
