// Logisim project step1alu.circ as structural Verilog: 8 circuits, main circuit top
module fulladd (
  input  in_1,
  input  in_2,
  input  in_3,
  output out_4,
  output out_5
);

  wire and_1_out, and_2_out, and_3_out;

  xor xor_1 (out_5, in_1, in_2, in_3);
  and and_1 (and_1_out, in_1, in_2);
  and and_2 (and_2_out, in_1, in_3);
  and and_3 (and_3_out, in_2, in_3);
  or or_1 (out_4, and_1_out, and_2_out, and_3_out);
endmodule

module add4 (
  input  [3:0] in_1,
  input  [3:0] in_2,
  input  in_3,
  output out_4,
  output [3:0] out_5
);

  wire fulladd_2_out_4, fulladd_3_out_4, fulladd_4_out_4;

  fulladd fulladd_1 (.in_1(in_1[3]), .in_2(in_2[3]), .in_3(fulladd_2_out_4), .out_4(out_4), .out_5(out_5[3]));
  fulladd fulladd_2 (.in_1(in_1[2]), .in_2(in_2[2]), .in_3(fulladd_3_out_4), .out_4(fulladd_2_out_4), .out_5(out_5[2]));
  fulladd fulladd_3 (.in_1(in_1[1]), .in_2(in_2[1]), .in_3(fulladd_4_out_4), .out_4(fulladd_3_out_4), .out_5(out_5[1]));
  fulladd fulladd_4 (.in_1(in_1[0]), .in_2(in_2[0]), .in_3(in_3), .out_4(fulladd_4_out_4), .out_5(out_5[0]));
endmodule

module flipper (
  input  in_1,
  input  in_2,
  input  in_3,
  input  in_4,
  input  in_5,
  output out_6,
  output out_7,
  output out_8,
  output out_9
);

  xor xor_1 (out_6, in_1, in_5);
  xor xor_2 (out_7, in_2, in_5);
  xor xor_3 (out_8, in_3, in_5);
  xor xor_4 (out_9, in_4, in_5);
endmodule

module ALU8 (
  input  lshr,
  input  lshl,
  input  \xor ,
  input  \or ,
  input  \and ,
  input  addsub,
  input  Subtract,
  input  [7:0] b,
  input  [7:0] a,
  output [7:0] x,
  output Cout
);

  wire [7:0] adder_1_out, and_1_out, bit_extender_1_out, leftshift8_1_out_2, or_1_out, rightshift8_1_out_2,
       xor_1_out, xor_2_out;

  assign bit_extender_1_out = {{7{Subtract}}, Subtract};  // Bit_Extender bit_extender_1
  assign xor_1_out = bit_extender_1_out ^ b;  // XOR_Gate xor_1, 8 bits wide
  Adder adder_1 (.a(xor_1_out), .b(a), .out(adder_1_out), .cin(Subtract), .cout(Cout));
  assign x = addsub ? adder_1_out : 8'bz;  // Controlled_Buffer controlled_buffer_1
  assign x = \and  ? and_1_out : 8'bz;  // Controlled_Buffer controlled_buffer_2
  assign and_1_out = b & a;  // AND_Gate and_1, 8 bits wide
  assign or_1_out = b | a;  // OR_Gate or_1, 8 bits wide
  assign x = \or  ? or_1_out : 8'bz;  // Controlled_Buffer controlled_buffer_3
  assign xor_2_out = b ^ a;  // XOR_Gate xor_2, 8 bits wide
  leftshift8 leftshift8_1 (.in_1(a), .out_2(leftshift8_1_out_2));
  rightshift8 rightshift8_1 (.in_1(a), .out_2(rightshift8_1_out_2));
  assign x = \xor  ? xor_2_out : 8'bz;  // Controlled_Buffer controlled_buffer_4
  assign x = lshl ? leftshift8_1_out_2 : 8'bz;  // Controlled_Buffer controlled_buffer_5
  assign x = lshr ? rightshift8_1_out_2 : 8'bz;  // Controlled_Buffer controlled_buffer_6
endmodule

module leftshift8 (
  input  [7:0] in_1,
  output [7:0] out_2
);


  assign out_2 = {in_1[6:0], 1'b0};
endmodule

module rightshift8 (
  input  [7:0] in_1,
  output [7:0] out_2
);


  assign out_2 = {1'b0, in_1[7:1]};
endmodule

module top (
  input  in_1,
  input  in_2,
  input  in_3,
  input  in_4,
  input  in_5,
  input  in_6,
  input  in_7,
  input  [7:0] in_8,
  input  in_9,
  input  in_10,
  input  enable,
  input  enable_2,
  input  in_13,
  input  in_14,
  input  in_15,
  input  in_16,
  input  clock,
  input  clear,
  output [7:0] out_19
);

  wire [7:0] controlled_buffer_1_out, controlled_buffer_2_out, register_1_q, register_2_q;

  assign controlled_buffer_1_out = in_9 ? in_8 : 8'bz;  // Controlled_Buffer controlled_buffer_1
  Register register_1 (.D(out_19), .en(enable), .Q(register_1_q), .clk(clock), .clr(clear));
  Register register_2 (.D(out_19), .en(enable_2), .Q(register_2_q), .clk(clock), .clr(clear));
  assign controlled_buffer_2_out = in_10 ? {8{1'b0}} : 8'bz;  // Controlled_Buffer controlled_buffer_2
  assign controlled_buffer_1_out = in_13 ? register_1_q : 8'bz;  // Controlled_Buffer controlled_buffer_3
  assign controlled_buffer_2_out = in_14 ? register_1_q : 8'bz;  // Controlled_Buffer controlled_buffer_4
  assign controlled_buffer_1_out = in_15 ? register_2_q : 8'bz;  // Controlled_Buffer controlled_buffer_5
  assign controlled_buffer_2_out = in_16 ? register_2_q : 8'bz;  // Controlled_Buffer controlled_buffer_6
  ALU8 alu8_1 (
    .lshr(in_1), .lshl(in_2), .\xor (in_3), .\or (in_4), .\and (in_5), .addsub(in_6), .Subtract(in_7),
    .b(controlled_buffer_1_out), .a(controlled_buffer_2_out), .x(out_19));  // open: Cout
endmodule

module latch1 (
  input  in_1,
  input  in_2,
  output out_3
);

  wire and_1_out, and_2_out, nor_1_out, not_1_out;

  and and_1 (and_1_out, in_1, in_2);
  and and_2 (and_2_out, in_2, not_1_out);
  not not_1 (not_1_out, in_1);
  nor nor_1 (nor_1_out, and_1_out, out_3);
  nor nor_2 (out_3, nor_1_out, and_2_out);
endmodule
