// Logisim project step3cu.circ as structural Verilog: 9 circuits, main circuit computer
module fulladd (
  input  in_1,
  input  in_2,
  input  in_3,
  output out_4,
  output out_5
);

  wire and_1_out, and_2_out, and_3_out;

  xor xor_1 (out_5, in_1, in_2, in_3);
  and and_1 (and_1_out, in_1, in_2);
  and and_2 (and_2_out, in_1, in_3);
  and and_3 (and_3_out, in_2, in_3);
  or or_1 (out_4, and_1_out, and_2_out, and_3_out);
endmodule

module add4 (
  input  [3:0] in_1,
  input  [3:0] in_2,
  input  in_3,
  output out_4,
  output [3:0] out_5
);

  wire fulladd_2_out_4, fulladd_3_out_4, fulladd_4_out_4;

  fulladd fulladd_1 (.in_1(in_1[3]), .in_2(in_2[3]), .in_3(fulladd_2_out_4), .out_4(out_4), .out_5(out_5[3]));
  fulladd fulladd_2 (.in_1(in_1[2]), .in_2(in_2[2]), .in_3(fulladd_3_out_4), .out_4(fulladd_2_out_4), .out_5(out_5[2]));
  fulladd fulladd_3 (.in_1(in_1[1]), .in_2(in_2[1]), .in_3(fulladd_4_out_4), .out_4(fulladd_3_out_4), .out_5(out_5[1]));
  fulladd fulladd_4 (.in_1(in_1[0]), .in_2(in_2[0]), .in_3(in_3), .out_4(fulladd_4_out_4), .out_5(out_5[0]));
endmodule

module flipper (
  input  in_1,
  input  in_2,
  input  in_3,
  input  in_4,
  input  in_5,
  output out_6,
  output out_7,
  output out_8,
  output out_9
);

  xor xor_1 (out_6, in_1, in_5);
  xor xor_2 (out_7, in_2, in_5);
  xor xor_3 (out_8, in_3, in_5);
  xor xor_4 (out_9, in_4, in_5);
endmodule

module ALU8 (
  input  lshr,
  input  lshl,
  input  \xor ,
  input  \or ,
  input  \and ,
  input  add,
  input  Subtract,
  input  [7:0] b,
  input  [7:0] a,
  output [7:0] x,
  output Cout,
  output out_12,
  output out_13
);

  wire adder_1_cout, leftshift8_1_out_2, or_1_out, rightshift8_1_out_2;
  wire [7:0] adder_1_out, and_1_out, bit_extender_1_out, leftshift8_1_out_3, or_2_out, rightshift8_1_out_3,
       xor_1_out, xor_2_out;

  assign bit_extender_1_out = {{7{Subtract}}, Subtract};  // Bit_Extender bit_extender_1
  assign xor_1_out = bit_extender_1_out ^ b;  // XOR_Gate xor_1, 8 bits wide
  or or_1 (or_1_out, add, Subtract);
  Adder adder_1 (.a(xor_1_out), .b(a), .out(adder_1_out), .cin(Subtract), .cout(adder_1_cout));
  assign {out_13, x[6:0]} = or_1_out ? adder_1_out : 8'bz;  // Controlled_Buffer controlled_buffer_1
  assign Cout = or_1_out ? adder_1_cout : 1'bz;  // Controlled_Buffer controlled_buffer_2
  assign and_1_out = b & a;  // AND_Gate and_1, 8 bits wide
  assign {out_13, x[6:0]} = \and  ? and_1_out : 8'bz;  // Controlled_Buffer controlled_buffer_3
  assign or_2_out = b | a;  // OR_Gate or_2, 8 bits wide
  assign {out_13, x[6:0]} = \or  ? or_2_out : 8'bz;  // Controlled_Buffer controlled_buffer_4
  assign xor_2_out = b ^ a;  // XOR_Gate xor_2, 8 bits wide
  leftshift8 leftshift8_1 (.in_1(a), .out_3(leftshift8_1_out_3), .out_2(leftshift8_1_out_2));
  rightshift8 rightshift8_1 (.in_1(a), .out_3(rightshift8_1_out_3), .out_2(rightshift8_1_out_2));
  assign Cout = lshl ? leftshift8_1_out_2 : 1'bz;  // Controlled_Buffer controlled_buffer_5
  assign {out_13, x[6:0]} = \xor  ? xor_2_out : 8'bz;  // Controlled_Buffer controlled_buffer_6
  assign {out_13, x[6:0]} = lshl ? leftshift8_1_out_3 : 8'bz;  // Controlled_Buffer controlled_buffer_7
  assign {out_13, x[6:0]} = lshr ? rightshift8_1_out_3 : 8'bz;  // Controlled_Buffer controlled_buffer_8
  assign Cout = lshr ? rightshift8_1_out_2 : 1'bz;  // Controlled_Buffer controlled_buffer_9
  nor nor_1 (out_12, x[0], x[1], x[2], x[3], x[5], x[6], out_13, x[4]);

  assign x[7] = out_13;
endmodule

module leftshift8 (
  input  [7:0] in_1,
  output out_2,
  output [7:0] out_3
);


  assign out_2 = in_1[7];
  assign out_3 = {in_1[6:0], 1'b0};
endmodule

module rightshift8 (
  input  [7:0] in_1,
  output out_2,
  output [7:0] out_3
);


  assign out_2 = in_1[0];
  assign out_3 = {1'b0, in_1[7:1]};
endmodule

// 1
module computer (
  input  in_1,
  input  in_2
);

  wire alu8_1_cout, alu8_1_out_12, alu8_1_out_13, and_1_out, and_2_out, and_3_out, controlled_buffer_1_out,
       d_ff_1_q, d_ff_2_q, d_ff_3_q, decoder_1_out0, decoder_1_out1, decoder_1_out2, decoder_1_out3,
       decoder_1_out4, decoder_1_out5, decoder_1_out6;
  wire [1:0] d_ff_4_q;
  wire [2:0] controlled_buffer_2_out_2, controlled_buffer_2_out_3, controlled_buffer_2_out_4,
       controlled_buffer_2_out_5, controlled_buffer_2_out_6;
  wire [5:0] not_1_out;
  wire [7:0] alu8_1_x, controlled_buffer_3_out, counter_1_q, multiplexer_1_out, multiplexer_2_out,
       multiplexer_3_out, register_1_q, register_2_q;
  wire [7:2] multiplexer_4_out;
  wire [20:0] controlled_buffer_2_out;

  Register register_1 (.D(alu8_1_x), .en(controlled_buffer_2_out[0]), .Q(register_1_q), .clk(in_2), .clr(in_1));
  Register register_2 (.D(alu8_1_x), .en(controlled_buffer_2_out[1]), .Q(register_2_q), .clk(in_2), .clr(in_1));
  Multiplexer #(.select(3), .width(8), .enable("false")) multiplexer_1 (
    .in0(register_1_q), .in1(register_2_q), .in2(controlled_buffer_3_out), .out(multiplexer_1_out),
    .sel(controlled_buffer_2_out_3));  // open: in3, in4, in5, in6, in7
  Multiplexer #(.select(3), .width(8), .enable("false")) multiplexer_2 (
    .in0(register_1_q), .in1(register_2_q), .in2({8{1'b0}}), .out(multiplexer_2_out),
    .sel(controlled_buffer_2_out_2));  // open: in3, in4, in5, in6, in7
  D_Flip_Flop d_ff_1 (.clk(in_2), .D(controlled_buffer_1_out), .Q(d_ff_1_q), .preset(in_1));  // open: Qn, en, reset
  Decoder #(.select(3), .enable("false")) decoder_1 (
    .out0(decoder_1_out0), .out1(decoder_1_out1), .out2(decoder_1_out2), .out3(decoder_1_out3),
    .out4(decoder_1_out4), .out5(decoder_1_out5), .out6(decoder_1_out6), .sel(controlled_buffer_2_out_4));  // open: out7
  assign controlled_buffer_1_out = and_2_out ? 1'b1 : 1'bz;  // Controlled_Buffer controlled_buffer_1
  Counter counter_1 (
    .load(controlled_buffer_2_out[15]), .D(alu8_1_x), .count(controlled_buffer_2_out[16]), .Q(counter_1_q),
    .clk(in_2), .clr(in_1));  // open: carry
  and and_1 (and_1_out, d_ff_1_q, ~controlled_buffer_1_out);  // AND_Gate
  not not_1 (not_1_out[0], not_1_out[1]);
  and and_2 (and_2_out, and_3_out, d_ff_1_q);
  assign {controlled_buffer_2_out[20], controlled_buffer_2_out_6, controlled_buffer_2_out[16:14], controlled_buffer_2_out_5, controlled_buffer_2_out_4, controlled_buffer_2_out_3, controlled_buffer_2_out_2, controlled_buffer_2_out[1:0]} = and_2_out ? {15'h5404, not_1_out[5], 3'b010, not_1_out[1:0]} : 21'bz;  // Controlled_Buffer controlled_buffer_2
  ALU8 alu8_1 (
    .lshr(decoder_1_out6), .lshl(decoder_1_out5), .\xor (decoder_1_out4), .\or (decoder_1_out3),
    .\and (decoder_1_out2), .add(decoder_1_out1), .Subtract(decoder_1_out0), .b(multiplexer_1_out),
    .a(multiplexer_2_out), .x(alu8_1_x), .Cout(alu8_1_cout), .out_12(alu8_1_out_12), .out_13(alu8_1_out_13));
  Multiplexer #(.select(3), .width(8), .enable("false")) multiplexer_3 (
    .in0(multiplexer_1_out), .in1(multiplexer_2_out), .in2(counter_1_q), .out(multiplexer_3_out),
    .sel(controlled_buffer_2_out_6));  // open: in3, in4, in5, in6, in7
  D_Flip_Flop d_ff_2 (
    .clk(in_2), .D(alu8_1_out_13), .Q(d_ff_2_q), .en(controlled_buffer_2_out_5[2]), .reset(in_1));  // open: Qn, preset
  D_Flip_Flop d_ff_3 (.clk(in_2), .D(and_1_out), .Q(d_ff_3_q), .reset(in_1));  // open: Qn, preset, en
  assign controlled_buffer_3_out = controlled_buffer_2_out[14] ? alu8_1_x : 8'bz;  // Controlled_Buffer controlled_buffer_3
  D_Flip_Flop d_ff_4 (
    .clk(in_2), .D(alu8_1_cout), .Q(d_ff_4_q[0]), .en(controlled_buffer_2_out_5[0]), .reset(in_1));  // open: Qn, preset
  D_Flip_Flop d_ff_5 (
    .clk(in_2), .D(alu8_1_out_12), .Q(d_ff_4_q[1]), .en(controlled_buffer_2_out_5[1]), .reset(in_1));  // open: Qn, preset
  RAM ram_1 (
    .addr(multiplexer_3_out), .data(controlled_buffer_3_out), .sel(1'b1), .clk(in_2),
    .ld(controlled_buffer_2_out[20]));  // open: clr
  Multiplexer #(.width(8), .enable("false")) multiplexer_4 (
    .in0(controlled_buffer_3_out), .in1({8{1'b0}}), .out({multiplexer_4_out, not_1_out[1], not_1_out[5]}),
    .sel(in_1));
  and and_3 (and_3_out, ~multiplexer_4_out[4], ~multiplexer_4_out[5], ~multiplexer_4_out[6], ~multiplexer_4_out[7]);  // AND_Gate

  // Notes on the sheet:
  //   PC
  //   Data Bus
endmodule

module latch1 (
  input  in_1,
  input  in_2,
  output out_3
);

  wire and_1_out, and_2_out, nor_1_out, not_1_out;

  and and_1 (and_1_out, in_1, in_2);
  and and_2 (and_2_out, in_2, not_1_out);
  not not_1 (not_1_out, in_1);
  nor nor_1 (nor_1_out, and_1_out, out_3);
  nor nor_2 (out_3, nor_1_out, and_2_out);
endmodule

module ram (
  input  in_1,
  input  [2:0] in_2,
  input  in_3,
  input  [7:0] in_4,
  input  in_5,
  input  in_6,
  output [7:0] out_7
);

  wire and_1_out, and_2_out, and_3_out, and_4_out, and_5_out, and_6_out, and_7_out, and_8_out, and_9_out,
       and_10_out, and_11_out, and_12_out, and_13_out, and_14_out, and_15_out, and_16_out, decoder_1_out0,
       decoder_1_out1, decoder_1_out2, decoder_1_out3, decoder_1_out4, decoder_1_out5, decoder_1_out6,
       decoder_1_out7;
  wire [7:0] register_1_q, register_2_q, register_3_q, register_4_q, register_5_q, register_6_q,
       register_7_q, register_8_q;

  Decoder #(.select(3)) decoder_1 (
    .out0(decoder_1_out0), .out1(decoder_1_out1), .out2(decoder_1_out2), .out3(decoder_1_out3),
    .out4(decoder_1_out4), .out5(decoder_1_out5), .out6(decoder_1_out6), .out7(decoder_1_out7), .sel(in_2),
    .en(in_1));
  and and_1 (and_1_out, ~in_5, decoder_1_out0);  // AND_Gate
  Register register_1 (.D(out_7), .en(and_1_out), .Q(register_1_q), .clk(in_3));  // open: clr
  and and_2 (and_2_out, decoder_1_out0, in_5);
  and and_3 (and_3_out, ~in_5, decoder_1_out1);  // AND_Gate
  Register register_2 (.D(out_7), .en(and_3_out), .Q(register_2_q), .clk(in_3));  // open: clr
  and and_4 (and_4_out, decoder_1_out1, in_5);
  and and_5 (and_5_out, ~in_5, decoder_1_out2);  // AND_Gate
  Register register_3 (.D(out_7), .en(and_5_out), .Q(register_3_q), .clk(in_3));  // open: clr
  and and_6 (and_6_out, decoder_1_out2, in_5);
  and and_7 (and_7_out, ~in_5, decoder_1_out3);  // AND_Gate
  Register register_4 (.D(out_7), .en(and_7_out), .Q(register_4_q), .clk(in_3));  // open: clr
  and and_8 (and_8_out, decoder_1_out3, in_5);
  and and_9 (and_9_out, ~in_5, decoder_1_out4);  // AND_Gate
  Register register_5 (.D(out_7), .en(and_9_out), .Q(register_5_q), .clk(in_3));  // open: clr
  and and_10 (and_10_out, decoder_1_out4, in_5);
  and and_11 (and_11_out, ~in_5, decoder_1_out5);  // AND_Gate
  Register register_6 (.D(out_7), .en(and_11_out), .Q(register_6_q), .clk(in_3));  // open: clr
  and and_12 (and_12_out, decoder_1_out5, in_5);
  and and_13 (and_13_out, ~in_5, decoder_1_out6);  // AND_Gate
  Register register_7 (.D(out_7), .en(and_13_out), .Q(register_7_q), .clk(in_3));  // open: clr
  and and_14 (and_14_out, decoder_1_out6, in_5);
  and and_15 (and_15_out, ~in_5, decoder_1_out7);  // AND_Gate
  Register register_8 (.D(out_7), .en(and_15_out), .Q(register_8_q), .clk(in_3));  // open: clr
  and and_16 (and_16_out, decoder_1_out7, in_5);
  assign out_7 = and_2_out ? register_1_q : 8'bz;  // Controlled_Buffer controlled_buffer_1
  assign out_7 = and_4_out ? register_2_q : 8'bz;  // Controlled_Buffer controlled_buffer_2
  assign out_7 = and_6_out ? register_3_q : 8'bz;  // Controlled_Buffer controlled_buffer_3
  assign out_7 = and_8_out ? register_4_q : 8'bz;  // Controlled_Buffer controlled_buffer_4
  assign out_7 = and_10_out ? register_5_q : 8'bz;  // Controlled_Buffer controlled_buffer_5
  assign out_7 = and_12_out ? register_6_q : 8'bz;  // Controlled_Buffer controlled_buffer_6
  assign out_7 = and_14_out ? register_7_q : 8'bz;  // Controlled_Buffer controlled_buffer_7
  assign out_7 = and_16_out ? register_8_q : 8'bz;  // Controlled_Buffer controlled_buffer_8
  assign out_7 = in_6 ? in_4 : 8'bz;  // Controlled_Buffer controlled_buffer_9

  // Notes on the sheet:
  //   read/write
endmodule
