// Logisim project stream2.circ as structural Verilog: 3 circuits, main circuit top
module fulladd (
  input  in_1,
  input  in_2,
  input  in_3,
  output out_4,
  output out_5
);

  wire and_1_out, and_2_out, and_3_out;

  xor xor_1 (out_5, in_1, in_2, in_3);
  and and_1 (and_1_out, in_1, in_2);
  and and_2 (and_2_out, in_1, in_3);
  and and_3 (and_3_out, in_2, in_3);
  or or_1 (out_4, and_1_out, and_2_out, and_3_out);
endmodule

module top (
  input  in_1,
  input  in_2,
  input  in_3,
  input  in_4,
  input  in_5,
  input  in_6,
  input  in_7,
  input  in_8,
  input  in_9,
  output out_10,
  output out_11,
  output out_12,
  output out_13,
  output out_14
);

  wire fulladd_1_out_4, fulladd_2_out_4, fulladd_3_out_4, fulladd_4_out_4, xor_1_out, xor_2_out, xor_3_out,
       xor_4_out;

  xor xor_1 (xor_1_out, in_5, in_9);
  xor xor_2 (xor_2_out, in_6, in_9);
  xor xor_3 (xor_3_out, in_7, in_9);
  xor xor_4 (xor_4_out, in_8, in_9);
  fulladd fulladd_1 (.in_1(in_1), .in_2(xor_1_out), .in_3(fulladd_2_out_4), .out_4(fulladd_1_out_4), .out_5(out_11));
  fulladd fulladd_2 (.in_1(in_2), .in_2(xor_2_out), .in_3(fulladd_3_out_4), .out_4(fulladd_2_out_4), .out_5(out_12));
  fulladd fulladd_3 (.in_1(in_3), .in_2(xor_3_out), .in_3(fulladd_4_out_4), .out_4(fulladd_3_out_4), .out_5(out_13));
  fulladd fulladd_4 (.in_1(in_4), .in_2(xor_4_out), .in_3(in_9), .out_4(fulladd_4_out_4), .out_5(out_14));
  xor xor_5 (out_10, fulladd_1_out_4, in_9);
endmodule

module flipper (
  input  in_1,
  input  in_2,
  input  in_3,
  input  in_4,
  input  in_5,
  output out_6,
  output out_7,
  output out_8,
  output out_9
);

  xor xor_1 (out_6, in_1, in_5);
  xor xor_2 (out_7, in_2, in_5);
  xor xor_3 (out_8, in_3, in_5);
  xor xor_4 (out_9, in_4, in_5);
endmodule
